# Fritzing sketch cablage_arduino_fritzing (saved by Fritzing 0.9.4)
breadboards: 2

parts:
  Composant1 = Arduino Mega 2560 (Rev3)
  Grove1 = Grove OLED 128x96
  P1 = S1133 Si Photodiode [package="8mm Ceramic [THT]"]
  S2 = Pushbutton [package="[THT]"]
  LED1 = RGB LED (com. anode, rbg) [package="5 mm [THT]"]
  LED2 = RGB LED (com. anode, rbg) [package="5 mm [THT]"]
  U1 = POT [package=pot_alpha_rv16af-20]  # not connected
  R1 = Resistor [tolerance=±5% resistance=220 package="0805 [SMD]"]
  IR1 = TSOP312.., 314.. [package=THT]  # not connected
  RHT1 = Humidity and Temperature Sensor RHT03
  R2 = Resistor [tolerance=±5% resistance=220 package=THT]
  U4 = LM 358 Dual Op-Amp [package="DIP8 [THT]"]
  U5 = OP27 - Low Noise, Precision Op Amp [part_number=OP27]
  P2 = S1133 Si Photodiode [package="8mm Ceramic [THT]"]
  R3 = Resistor [tolerance=±5% resistance=24k package="2512 [SMD]"]
  R4 = Resistor [tolerance=±5% resistance=220k package="2512 [SMD]"]
  R5 = Resistor [tolerance=±5% resistance=100 package="2512 [SMD]"]
  R6 = Resistor [tolerance=±5% resistance=220 package=THT]
  R7 = Resistor [tolerance=±5% resistance=220 package=THT]
  R8 = Resistor [tolerance=±5% resistance=220 package=THT]

nets:
  N1: Composant1.A0, U4.connector0, R4.Pin_0
  VCC: Composant1.5V, Grove1.VCC, LED1.common_anode, LED2.common_anode, RHT1.Vcc, R2.Pin_0, U4.connector7, U5.V+
  GND: Composant1.GND, Composant1.D4_PWM, Grove1.GND, P1.anode, S2.Pin_3, S2.Pin_4, RHT1.GND_2, U4.connector3, U5.+IN, U5.-V, P2.cathode, R3.Pin_1
  N2: Composant1.D2_PWM, R1.Pin_0
  N3: Composant1.D3_PWM, RHT1.GND_1
  N4: Composant1.D5_PWM, R6.Pin_1
  N5: Composant1.D6_PWM, R7.Pin_1
  N6: Composant1.D7_PWM, R8.Pin_1
  N7: P1.cathode, R1.Pin_1
  N8: S2.Pin_1, S2.Pin_2
  N9: LED1.red_cathode, LED2.red_cathode, R6.Pin_0
  N10: LED1.blue_cathode, LED2.blue_cathode, R7.Pin_0
  N11: LED1.green_cathode, LED2.green_cathode, R8.Pin_0
  N12: RHT1.Data-signal, R2.Pin_1
  N13: U4.connector1, R3.Pin_0, R4.Pin_1
  N14: U5.-IN, P2.anode
  N15: U5.OUT, R5.Pin_0
