# Fritzing sketch cablage_plaques_cuivres (saved by Fritzing 0.9.3b)
stripboards: 10

parts:
  Part1 = Arduino Mega 2560 (Rev3)
  LED1 = RGB LED (com. cathode, rgb) [package="5 mm [THT]"]
  LED2 = RGB LED (com. cathode, rgb) [package="5 mm [THT]"]
  LED3 = RGB LED (com. cathode, rgb) [package="5 mm [THT]"]
  LED4 = RGB LED (com. cathode, rgb) [package="5 mm [THT]"]

nets:
  3V3: Part1.3V3, Part1.5V
  N1: LED1.red_anode, LED2.blue_anode, LED3.red_anode, LED4.blue_anode
  N2: LED1.common_cathode, LED3.common_cathode
  N3: LED1.green_anode, LED3.green_anode
  N4: LED1.blue_anode, LED3.blue_anode
  N5: LED2.red_anode, LED4.red_anode
  N6: LED2.common_cathode, LED4.common_cathode
  N7: LED2.green_anode, LED4.green_anode

notes:
  OLED
  LED RGB
  Module LEDs
